// Logisim project Exercitiul 1.circ as structural Verilog: 1 circuit, main circuit main
module main (
  input  I,
  input  S1,
  input  S0,
  output O0,
  output O1,
  output O2,
  output O3
);

  wire not_1_out, not_2_out;

  not not_1 (not_1_out, S1);
  not not_2 (not_2_out, S0);
  and and_1 (O0, I, not_1_out, not_2_out);
  and and_2 (O1, I, not_2_out, S1);
  and and_3 (O2, I, S0, not_1_out);
  and and_4 (O3, I, S1, S0);
endmodule
