// Logisim project Ex 2.circ as structural Verilog: 1 circuit, main circuit main
module main (
  input  a2,
  input  a1,
  input  a0,
  output d2,
  output d1,
  output d0
);

  wire not_1_out;

  not not_1 (not_1_out, a0);
  and and_1 (d2, not_1_out, a0);

  assign d0 = a1;
  assign d1 = a2;
endmodule
