// Logisim project Ex 4.circ as structural Verilog: 1 circuit, main circuit main
module main (
  input  x1,
  input  x2,
  output f1,
  output f2
);

  xor xor_1 (f1, x1, x2);
  not not_1 (f2, x2);
endmodule
