// Logisim project Circuit 1 (2021_03_22 15_14_12 UTC).circ as structural Verilog: 1 circuit, main circuit main
module main (
  input  a0,
  input  b0,
  output s0,
  output T0
);

  and and_1 (T0, a0, b0);
  xor xor_1 (s0, a0, b0);
endmodule
