// Logisim project Circuit 3 (2021_03_22 18_47_05 UTC).circ as structural Verilog: 1 circuit, main circuit main
module main (
  input  ai,
  input  bi,
  input  Ti_1_Ii_1,
  input  _0_1_c,
  output si,
  output Ti___Ii
);

  wire and_1_out, and_2_out, xor_1_out, xor_2_out, xor_4_out;

  xor xor_1 (xor_1_out, ai, bi);
  xor xor_2 (xor_2_out, ai, _0_1_c);
  xor xor_3 (si, xor_1_out, Ti_1_Ii_1);
  and and_1 (and_1_out, xor_2_out, bi);
  xor xor_4 (xor_4_out, xor_1_out, _0_1_c);
  and and_2 (and_2_out, xor_4_out, Ti_1_Ii_1);
  or or_1 (Ti___Ii, and_1_out, and_2_out);
endmodule
