// Logisim project Ex 1.circ as structural Verilog: 1 circuit, main circuit main
module main (
  input  a,
  input  b,
  input  c,
  output out_4,
  output out_5,
  output out_6,
  output out_7,
  output out_8,
  output out_9,
  output out_10,
  output out_11
);

  wire not_1_out;

  not not_1 (not_1_out, a);
  Decoder #(.select(2)) decoder_1 (
    .out0(out_4), .out1(out_5), .out2(out_6), .out3(out_7), .sel({c, b}), .en(not_1_out));
  Decoder #(.select(2)) decoder_2 (.out0(out_8), .out1(out_9), .out2(out_10), .out3(out_11), .sel({c, b}), .en(a));
endmodule
