// Logisim project Ex 5.circ as structural Verilog: 1 circuit, main circuit main
module main (
  input  x1,
  input  x2,
  input  c,
  output f1,
  output f2
);

  wire xor_1_out;

  not not_1 (f2, x2);
  xor xor_1 (xor_1_out, x1, x2);
  xor xor_2 (f1, xor_1_out, c);
endmodule
